# Fritzing sketch proiect_pm (saved by Fritzing 0.9.3b)
breadboards: 1

parts:
  Part1 = Arduino Uno (Rev3) - ICSP
  U1 = LCD-16X2 [package=lcd-16x2_noholes]
  Part2 = MicroSD Card Module
  R1 = TRIMPOT [package=trimpot-3mm]
  R2 = Resistor [tolerance=±5% resistance=220 package=THT]
  LEFT_RED = Pushbutton [package="[THT]"]
  LEFT_BLUE = Pushbutton [package="[THT]"]
  LEFT_YELLOW = Pushbutton [package="[THT]"]
  RIGHT_RED = Pushbutton [package="[THT]"]
  RIGHT_YELLOW = Pushbutton [package="[THT]"]
  RIGHT_BLUE = Pushbutton [package="[THT]"]
  R3 = Resistor [tolerance=±5% resistance=220 package=THT]
  R4 = Resistor [tolerance=±5% resistance=220 package=THT]
  R5 = Resistor [tolerance=±5% resistance=220 package=THT]
  R6 = Resistor [tolerance=±5% resistance=220 package=THT]
  R7 = Resistor [tolerance=±5% resistance=220 package=THT]
  R8 = Resistor [tolerance=±5% resistance=220 package=THT]
  R9 = Resistor [tolerance=±5% resistance=220 package=THT]
  WHITE = Pushbutton [package="[THT]"]
  RED_LED = LED - 5mm [color="Red (633nm)" package="5 mm [THT]"]
  YELLOW_LED = LED - 5mm [color="Yellow (595nm)" package="5 mm [THT]"]
  BLUE_LED = LED - 5mm [color="Blue (525nm)" package="5 mm [THT]"]
  R10 = Resistor [tolerance=±5% resistance=220 package=THT]
  R11 = Resistor [tolerance=±5% resistance=220 package=THT]
  R12 = Resistor [tolerance=±5% resistance=220 package=THT]

nets:
  N1: Part1.A0, LEFT_RED.Pin_4, LEFT_BLUE.Pin_4, LEFT_YELLOW.Pin_3, LEFT_YELLOW.Pin_4, RIGHT_RED.Pin_3, RIGHT_RED.Pin_4, RIGHT_YELLOW.Pin_4, RIGHT_BLUE.Pin_3, RIGHT_BLUE.Pin_4
  N2: Part1.A1, R11.Pin_0
  N3: Part1.ICSP_MISO, Part1.D12/MISO, Part2.MISO
  5V: Part1.5V, U1.VDD, Part2.VCC, R1.CCW, R2.Pin_0, R9.Pin_1
  N4: Part1.ICSP_SCK, Part1.D13/SCK, Part2.SCK
  N5: Part1.ICSP_MOSI, Part1.D11_PWM/MOSI, Part2.MOSI
  GND: Part1.GND, U1.VSS, U1.R_W, U1.K, Part2.GND, R1.CW, R3.Pin_0, WHITE.Pin_3, WHITE.Pin_4
  N6: Part1.D8, U1.RS
  N7: Part1.D10_PWM/SS, Part2.CS
  N8: Part1.D2, U1.DB7
  N9: Part1.D3_PWM, U1.DB6
  N10: Part1.D4, WHITE.Pin_1, WHITE.Pin_2
  N11: Part1.D5_PWM, U1.DB4
  N12: Part1.D6_PWM, U1.DB5
  N13: Part1.D7, U1.E
  N14: U1.VO, R1.WIPER
  N15: U1.A, R2.Pin_1
  N16: R3.Pin_1, R4.Pin_0
  N17: R4.Pin_1, R5.Pin_0
  N18: R5.Pin_1, R6.Pin_0
  N19: R6.Pin_1, R7.Pin_0
  N20: R7.Pin_1, R8.Pin_0
  N21: R8.Pin_1, R9.Pin_0
  N22: RED_LED.cathode, R10.Pin_1
  N23: YELLOW_LED.cathode, R11.Pin_1
  N24: BLUE_LED.cathode, R12.Pin_1
  A3: R10.Pin_0
  A2: R12.Pin_0
